# Fritzing sketch +áema spajanja (saved by Fritzing 0.9.3b)
breadboards: 1

parts:
  Part1 = SRF05 Ultrasonic Rangefinder
  SERVO1 = Tower Pro SG90 servo [part_number=101246]
  LCD1 = TFT 1.8 inch 160x128 w SD  # not connected
  Mod1 = Raspberry Pi Pico
  R1 = Resistor [tolerance=±5% resistance=220 package=THT]
  R2 = Resistor [tolerance=±5% resistance=220 package=THT]

nets:
  N1: Part1.Trig, Mod1.pin_32
  N2: Part1.Echo, R2.Pin_1
  GND: Part1.GND, SERVO1.GND, Mod1.pin_3, Mod1.pin_13, Mod1.pin_23, Mod1.pin_33, Mod1.pin_42, R1.Pin_0
  N3: SERVO1.Signal, Mod1.pin_34
  N4: SERVO1.+5V, Mod1.pin_36
  N5: Mod1.pin_31, R1.Pin_1, R2.Pin_0

custom parts:
  Tower Pro SG90 servo: Original file by John De Cristofaro http://www.adafruit.com/products/1449 Adafruit Feedback Servo (Small) Edited by: e-radionica.com 28/9/2015
  TFT 1.8 inch 160x128 w SD: This is a generic 1.8 tft spi lcd display available on ebay and others. The 1.8" display has 128x160 color pixels.
  Raspberry Pi Pico: Raspberry Pi Pico. Based around the RP2040 microcontroller the Pico is a low cost microcontroller device bringing Raspberry Pi quality, cost, and easy of use to the microcontroller space. Jan 2021, Split part in to two versions: tht (this one) and SMD. This one will drill holes for a .1 in header in pcb to allow plugging in the module as well as providing pads to solder the module to the top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
